// Logisim project ALU.circ as structural Verilog: 11 circuits, main circuit aluk
module aluk (
  input  [7:0] A,
  input  [7:0] B,
  input  [2:0] OpCode,
  output [7:0] Result,
  output Zero,
  output Carry
);

  wire add_1_over, and_1_out, and_2_out, and_3_out, and_4_out, and_5_out, and_6_out, and_7_out, not_1_out,
       not_2_out, not_3_out, not_4_out, or_1_out, or_2_out, shift_1_over, shift_1_rover;
  wire [7:0] add_1_re, andd_1_re, decorderr_1_opc, orr_1_re, pass_1_apass, shift_1_r0, shift_1_re0,
       xork_1_ib, xorr_1_re;

  or or_1 (or_1_out, decorderr_1_opc[1], not_1_out);
  or or_2 (or_2_out, and_1_out, and_3_out);
  not not_1 (not_1_out, decorderr_1_opc[0]);
  and and_1 (and_1_out, not_2_out, decorderr_1_opc[1]);
  not not_2 (not_2_out, decorderr_1_opc[0]);
  and and_2 (and_2_out, or_1_out, or_2_out);
  and and_3 (and_3_out, decorderr_1_opc[0], not_3_out);
  not not_3 (not_3_out, decorderr_1_opc[1]);
  Decorderr decorderr_1 (.Op(OpCode), .Opc(decorderr_1_opc));
  Xork xork_1 (.B(B), .Source(and_2_out), .ib(xork_1_ib));
  Add add_1 (.Sub(and_2_out), .A(A), .B(xork_1_ib), .Source(or_2_out), .Re(add_1_re), .Over(add_1_over));
  Andd andd_1 (.A(A), .B(B), .Source(decorderr_1_opc[2]), .Re(andd_1_re));
  Orr orr_1 (.A(A), .B(B), .Source(decorderr_1_opc[3]), .Re(orr_1_re));
  Xorr xorr_1 (.A(A), .B0(B), .Source(decorderr_1_opc[4]), .Re(xorr_1_re));
  Pass pass_1 (.A(A), .Source(decorderr_1_opc[7]), .Apass(pass_1_apass));
  Shift shift_1 (
    .A(A), .Left(decorderr_1_opc[5]), .Right(decorderr_1_opc[6]), .Re0(shift_1_re0[0]), .Re1(shift_1_re0[1]),
    .Re2(shift_1_re0[2]), .Re3(shift_1_re0[3]), .Re4(shift_1_re0[4]), .Re5(shift_1_re0[5]),
    .Re6(shift_1_re0[6]), .Re7(shift_1_re0[7]), .Over(shift_1_over), .Rover(shift_1_rover),
    .R0(shift_1_r0[0]), .R1(shift_1_r0[1]), .R2(shift_1_r0[2]), .R3(shift_1_r0[3]), .R4(shift_1_r0[4]),
    .R5(shift_1_r0[5]), .R6(shift_1_r0[6]), .R7(shift_1_r0[7]));
  assign Result = add_1_re | andd_1_re | orr_1_re | xorr_1_re | pass_1_apass | shift_1_re0 | shift_1_r0;  // OR_Gate or_3, 8 bits wide
  not not_4 (not_4_out, add_1_over);
  and and_4 (and_4_out, decorderr_1_opc[0], add_1_over);
  and and_5 (and_5_out, decorderr_1_opc[1], not_4_out);
  and and_6 (and_6_out, decorderr_1_opc[5], shift_1_over);
  and and_7 (and_7_out, decorderr_1_opc[6], shift_1_rover);
  Zflag zflag_1 (.in_1(Result), .out_2(Zero));
  or or_4 (Carry, and_4_out, and_5_out, and_6_out, and_7_out);
endmodule

module Add (
  input  Sub,
  input  [7:0] A,
  input  [7:0] B,
  input  Source,
  output [7:0] Re,
  output Over
);

  wire add2_1_cout, add2_1_re, add2_2_cout, add2_2_re, add2_3_cout, add2_3_re, add2_4_cout, add2_4_re,
       add2_5_cout, add2_5_re, add2_6_cout, add2_6_re, add2_7_cout, add2_7_re, add2_8_re;

  add2 add2_1 (.Cin(Sub), .A(A[0]), .B(B[0]), .Re(add2_1_re), .Cout(add2_1_cout));
  add2 add2_2 (.Cin(add2_1_cout), .A(A[1]), .B(B[1]), .Re(add2_2_re), .Cout(add2_2_cout));
  add2 add2_3 (.Cin(add2_2_cout), .A(A[2]), .B(B[2]), .Re(add2_3_re), .Cout(add2_3_cout));
  add2 add2_4 (.Cin(add2_3_cout), .A(A[3]), .B(B[3]), .Re(add2_4_re), .Cout(add2_4_cout));
  add2 add2_5 (.Cin(add2_4_cout), .A(A[4]), .B(B[4]), .Re(add2_5_re), .Cout(add2_5_cout));
  add2 add2_6 (.Cin(add2_5_cout), .A(A[5]), .B(B[5]), .Re(add2_6_re), .Cout(add2_6_cout));
  add2 add2_7 (.Cin(add2_6_cout), .A(A[6]), .B(B[6]), .Re(add2_7_re), .Cout(add2_7_cout));
  add2 add2_8 (.Cin(add2_7_cout), .A(A[7]), .B(B[7]), .Re(add2_8_re), .Cout(Over));
  and and_1 (Re[0], add2_1_re, Source);
  and and_2 (Re[1], add2_2_re, Source);
  and and_3 (Re[2], add2_3_re, Source);
  and and_4 (Re[3], add2_4_re, Source);
  and and_5 (Re[4], add2_5_re, Source);
  and and_6 (Re[5], add2_6_re, Source);
  and and_7 (Re[6], add2_7_re, Source);
  and and_8 (Re[7], add2_8_re, Source);
endmodule

module add2 (
  input  Cin,
  input  A,
  input  B,
  output Re,
  output Cout
);

  wire and_1_out, and_2_out, or_1_out, xor_1_out;

  xor xor_1 (xor_1_out, A, B);
  and and_1 (and_1_out, B, A);
  or or_1 (or_1_out, B, A);
  xor xor_2 (Re, Cin, xor_1_out);
  and and_2 (and_2_out, Cin, or_1_out);
  or or_2 (Cout, and_1_out, and_2_out);
endmodule

module Xork (
  input  [7:0] B,
  input  Source,
  output [7:0] ib
);

  xor xor_1 (ib[0], B[0], Source);
  xor xor_2 (ib[1], B[1], Source);
  xor xor_3 (ib[2], B[2], Source);
  xor xor_4 (ib[3], B[3], Source);
  xor xor_5 (ib[4], B[4], Source);
  xor xor_6 (ib[5], B[5], Source);
  xor xor_7 (ib[6], B[6], Source);
  xor xor_8 (ib[7], B[7], Source);
endmodule

module Andd (
  input  [7:0] A,
  input  [7:0] B,
  input  Source,
  output [7:0] Re
);

  and and_1 (Re[0], A[0], B[0], Source);
  and and_2 (Re[1], A[1], B[1], Source);
  and and_3 (Re[2], A[2], B[2], Source);
  and and_4 (Re[3], A[3], B[3], Source);
  and and_5 (Re[4], A[4], B[4], Source);
  and and_6 (Re[5], A[5], B[5], Source);
  and and_7 (Re[6], A[6], B[6], Source);
  and and_8 (Re[7], A[7], B[7], Source);
endmodule

module Orr (
  input  [7:0] A,
  input  [7:0] B,
  input  Source,
  output [7:0] Re
);

  wire or_1_out, or_2_out, or_3_out, or_4_out, or_5_out, or_6_out, or_7_out, or_8_out;

  or or_1 (or_1_out, A[0], B[0]);
  and and_1 (Re[0], or_1_out, Source);
  or or_2 (or_2_out, A[1], B[1]);
  and and_2 (Re[1], or_2_out, Source);
  or or_3 (or_3_out, A[2], B[2]);
  and and_3 (Re[2], or_3_out, Source);
  or or_4 (or_4_out, A[3], B[3]);
  and and_4 (Re[3], or_4_out, Source);
  or or_5 (or_5_out, A[4], B[4]);
  and and_5 (Re[4], or_5_out, Source);
  or or_6 (or_6_out, A[5], B[5]);
  and and_6 (Re[5], or_6_out, Source);
  or or_7 (or_7_out, A[6], B[6]);
  and and_7 (Re[6], or_7_out, Source);
  or or_8 (or_8_out, A[7], B[7]);
  and and_8 (Re[7], or_8_out, Source);
endmodule

module Xorr (
  input  [7:0] A,
  input  [7:0] B0,
  input  Source,
  output [7:0] Re
);

  wire xor_1_out, xor_2_out, xor_3_out, xor_4_out, xor_5_out, xor_6_out, xor_7_out, xor_8_out;

  xor xor_1 (xor_1_out, A[0], B0[0]);
  and and_1 (Re[0], xor_1_out, Source);
  xor xor_2 (xor_2_out, A[1], B0[1]);
  and and_2 (Re[1], xor_2_out, Source);
  xor xor_3 (xor_3_out, A[2], B0[2]);
  and and_3 (Re[2], xor_3_out, Source);
  xor xor_4 (xor_4_out, A[3], B0[3]);
  and and_4 (Re[3], xor_4_out, Source);
  xor xor_5 (xor_5_out, A[4], B0[4]);
  and and_5 (Re[4], xor_5_out, Source);
  xor xor_6 (xor_6_out, A[5], B0[5]);
  and and_6 (Re[5], xor_6_out, Source);
  xor xor_7 (xor_7_out, A[6], B0[6]);
  and and_7 (Re[6], xor_7_out, Source);
  xor xor_8 (xor_8_out, A[7], B0[7]);
  and and_8 (Re[7], xor_8_out, Source);
endmodule

module Shift (
  input  [7:0] A,
  input  Left,
  input  Right,
  output Re0,
  output Re1,
  output Re2,
  output Re3,
  output Re4,
  output Re5,
  output Re6,
  output Re7,
  output Over,
  output Rover,
  output R0,
  output R1,
  output R2,
  output R3,
  output R4,
  output R5,
  output R6,
  output R7
);

  wire undriven;

  and and_1 (Re1, A[0], Left);
  and and_2 (Rover, A[0], Right);
  and and_3 (Re2, A[1], Left);
  and and_4 (R0, A[1], Right);
  and and_5 (Re3, A[2], Left);
  and and_6 (R1, A[2], Right);
  and and_7 (Re4, A[3], Left);
  and and_8 (R2, A[3], Right);
  and and_9 (Re5, A[4], Left);
  and and_10 (R3, A[4], Right);
  and and_11 (Re6, A[5], Left);
  and and_12 (R4, A[5], Right);
  and and_13 (Re7, A[6], Left);
  and and_14 (R5, A[6], Right);
  and and_15 (Over, undriven, Left);
  and and_16 (R6, undriven, Right);
  not not_1 (Re0, 1'b1);
  not not_2 (R7, 1'b1);
endmodule

module Pass (
  input  [7:0] A,
  input  Source,
  output [7:0] Apass
);

  and and_1 (Apass[0], A[0], Source);
  and and_2 (Apass[1], A[1], Source);
  and and_3 (Apass[2], A[2], Source);
  and and_4 (Apass[3], A[3], Source);
  and and_5 (Apass[4], A[4], Source);
  and and_6 (Apass[5], A[5], Source);
  and and_7 (Apass[6], A[6], Source);
  and and_8 (Apass[7], A[7], Source);
endmodule

module Decorderr (
  input  [2:0] Op,
  output [7:0] Opc
);

  wire not_1_out, not_2_out, not_3_out;

  not not_1 (not_1_out, Op[0]);
  not not_2 (not_2_out, Op[1]);
  not not_3 (not_3_out, Op[2]);
  and and_1 (Opc[7], Op[0], Op[1], Op[2]);
  and and_2 (Opc[6], not_1_out, Op[1], Op[2]);
  and and_3 (Opc[5], Op[0], not_2_out, Op[2]);
  and and_4 (Opc[4], not_2_out, not_1_out, Op[2]);
  and and_5 (Opc[3], not_3_out, Op[0], Op[1]);
  and and_6 (Opc[2], not_1_out, Op[1], not_3_out);
  and and_7 (Opc[1], not_3_out, not_2_out, Op[0]);
  and and_8 (Opc[0], not_1_out, not_2_out, not_3_out);
endmodule

module Zflag (
  input  [7:0] in_1,
  output out_2
);

  wire or_1_out;

  // NOT_Gate not_1 has open pins: in={8{1'b1}}, out=open
  or or_1 (or_1_out, in_1[0], in_1[1], in_1[2], in_1[3], in_1[4], in_1[5], in_1[6], in_1[7]);
  not not_2 (out_2, or_1_out);
endmodule
