// Logisim project BCDsegment.circ as structural Verilog: 8 circuits, main circuit Seg
module Seg (
  input  [3:0] in_1,
  input  [3:0] in_2
);

  wire a_1_ay, b_1_by, c_1_cy, d_1_dy, e_1_ey, f_1_fy, g_1_gy;

  Hex_Digit_Display hex_digit_display_1 (.value(in_1));  // open: dp
  A a_1 (.AL(in_2[0]), .BL(in_2[1]), .CL(in_2[2]), .DL(in_2[3]), .AY(a_1_ay));
  B b_1 (.AL(in_2[0]), .BL(in_2[1]), .CL(in_2[2]), .DL(in_2[3]), .BY(b_1_by));
  C c_1 (.AL(in_2[0]), .BL(in_2[1]), .CL(in_2[2]), .DL(in_2[3]), .CY(c_1_cy));
  D d_1 (.AL(in_2[0]), .BL(in_2[1]), .CL(in_2[2]), .DL(in_2[3]), .DY(d_1_dy));
  E e_1 (.AL(in_2[0]), .BL(in_2[1]), .CL(in_2[2]), .DL(in_2[3]), .EY(e_1_ey));
  F f_1 (.AL(in_2[0]), .BL(in_2[1]), .CL(in_2[2]), .DL(in_2[3]), .FY(f_1_fy));
  G g_1 (.AL(in_2[0]), .BL(in_2[1]), .CL(in_2[2]), .DL(in_2[3]), .GY(g_1_gy));
  _7_Segment_Display u_7_segment_display_1 (
    .g(g_1_gy), .f(f_1_fy), .a(a_1_ay), .b(b_1_by), .e(e_1_ey), .d(d_1_dy), .c(c_1_cy));  // open: dp
endmodule

module A (
  input  AL,
  input  BL,
  input  CL,
  input  DL,
  output AY
);

  wire and_1_out, and_2_out, and_3_out, not_1_out, not_2_out, not_3_out, not_4_out, or_1_out;

  not not_1 (not_1_out, AL);
  not not_2 (not_2_out, BL);
  not not_3 (not_3_out, CL);
  not not_4 (not_4_out, DL);
  and and_1 (and_1_out, not_1_out, not_2_out);
  and and_2 (and_2_out, not_4_out, CL, AL);
  or or_1 (or_1_out, and_1_out, DL);
  and and_3 (and_3_out, or_1_out, not_3_out);
  or or_2 (AY, BL, and_2_out, and_3_out);
endmodule

module B (
  input  AL,
  input  BL,
  input  CL,
  input  DL,
  output BY
);

  wire and_1_out, and_2_out, and_3_out, and_4_out, and_5_out, not_1_out, not_2_out, not_3_out, not_4_out,
       or_1_out, or_2_out;

  not not_1 (not_1_out, AL);
  not not_2 (not_2_out, BL);
  not not_3 (not_3_out, CL);
  not not_4 (not_4_out, DL);
  and and_1 (and_1_out, DL, not_2_out);
  and and_2 (and_2_out, AL, BL);
  and and_3 (and_3_out, not_1_out, not_2_out);
  or or_1 (or_1_out, and_2_out, and_3_out);
  or or_2 (or_2_out, not_4_out, and_1_out);
  and and_4 (and_4_out, not_4_out, or_1_out);
  and and_5 (and_5_out, not_3_out, or_2_out);
  or or_3 (BY, and_4_out, and_5_out);
endmodule

module C (
  input  AL,
  input  BL,
  input  CL,
  input  DL,
  output CY
);

  wire and_1_out, and_2_out, and_3_out, not_1_out, not_2_out, not_3_out, or_1_out;

  not not_1 (not_1_out, BL);
  not not_2 (not_2_out, CL);
  not not_3 (not_3_out, DL);
  and and_1 (and_1_out, AL, BL);
  or or_1 (or_1_out, CL, and_1_out);
  and and_2 (and_2_out, not_1_out, not_2_out);
  and and_3 (and_3_out, not_3_out, or_1_out);
  or or_2 (CY, and_2_out, and_3_out);
endmodule

module D (
  input  AL,
  input  BL,
  input  CL,
  input  DL,
  output DY
);

  wire and_1_out, and_2_out, and_3_out, and_4_out, not_1_out, not_2_out, not_3_out, not_4_out, or_1_out,
       or_2_out, or_3_out;

  not not_1 (not_1_out, AL);
  not not_2 (not_2_out, BL);
  not not_3 (not_3_out, CL);
  not not_4 (not_4_out, DL);
  and and_1 (and_1_out, AL, not_4_out, CL);
  and and_2 (and_2_out, or_1_out, not_3_out);
  or or_1 (or_1_out, not_1_out, DL);
  or or_2 (or_2_out, not_1_out, not_3_out);
  and and_3 (and_3_out, not_4_out, BL, or_2_out);
  or or_3 (or_3_out, and_2_out, and_1_out);
  or or_4 (DY, and_4_out, and_3_out);
  and and_4 (and_4_out, not_2_out, or_3_out);
endmodule

module E (
  input  AL,
  input  BL,
  input  CL,
  input  DL,
  output EY
);

  wire and_1_out, and_2_out, not_1_out, not_2_out, not_3_out, not_4_out, or_1_out;

  not not_1 (not_1_out, AL);
  not not_2 (not_2_out, BL);
  not not_3 (not_3_out, CL);
  not not_4 (not_4_out, DL);
  and and_1 (and_1_out, not_2_out, not_3_out);
  and and_2 (and_2_out, BL, not_4_out);
  and and_3 (EY, not_1_out, or_1_out);
  or or_1 (or_1_out, and_1_out, and_2_out);
endmodule

module F (
  input  AL,
  input  BL,
  input  CL,
  input  DL,
  output FY
);

  wire and_1_out, and_2_out, not_1_out, not_2_out, not_3_out, not_4_out, or_1_out, or_3_out;

  not not_1 (not_1_out, AL);
  not not_2 (not_2_out, BL);
  not not_3 (not_3_out, CL);
  not not_4 (not_4_out, DL);
  and and_1 (and_1_out, not_4_out, CL, or_1_out);
  or or_1 (or_1_out, not_1_out, not_2_out);
  or or_2 (FY, and_2_out, and_1_out);
  or or_3 (or_3_out, not_1_out, DL);
  and and_2 (and_2_out, not_2_out, or_3_out, not_3_out);
endmodule

module G (
  input  AL,
  input  BL,
  input  CL,
  input  DL,
  output GY
);

  wire and_1_out, and_2_out, and_3_out, and_4_out, not_1_out, not_2_out, not_3_out, not_4_out, or_1_out,
       or_2_out;

  or or_1 (or_1_out, not_2_out, not_1_out);
  not not_1 (not_1_out, AL);
  not not_2 (not_2_out, BL);
  not not_3 (not_3_out, CL);
  not not_4 (not_4_out, DL);
  and and_1 (and_1_out, BL, not_4_out);
  or or_2 (or_2_out, and_1_out, and_4_out);
  and and_2 (and_2_out, or_1_out, CL, not_4_out);
  and and_3 (and_3_out, not_3_out, or_2_out);
  and and_4 (and_4_out, not_2_out, DL);
  or or_3 (GY, and_2_out, and_3_out);
endmodule
