// Logisim project Full Adder.circ as structural Verilog: 1 circuit, main circuit main
module main (
  input  A1,
  input  A0,
  input  A7,
  input  A6,
  input  A5,
  input  A4,
  input  A3,
  input  A2,
  input  B1,
  input  B0,
  input  B7,
  input  B6,
  input  B5,
  input  B4,
  input  B3,
  input  B2
);

  wire and_1_out, and_2_out, and_3_out, and_4_out, and_5_out, and_6_out, and_7_out, and_8_out, and_9_out,
       and_10_out, and_11_out, and_12_out, and_13_out, and_14_out, and_15_out, and_16_out, and_17_out,
       and_18_out, and_19_out, not_1_out, not_2_out, not_3_out, not_4_out, not_5_out, not_6_out, not_7_out,
       not_8_out, or_1_out, or_2_out, or_3_out, or_4_out, or_5_out, or_6_out, or_7_out, or_8_out, or_9_out,
       or_10_out, or_11_out, or_12_out, or_13_out, or_14_out, or_15_out, or_16_out, or_17_out, or_18_out,
       or_19_out, or_20_out, xor_1_out, xor_2_out, xor_3_out, xor_4_out, xor_5_out, xor_6_out, xor_7_out,
       xor_8_out, xor_9_out, xor_10_out, xor_11_out, xor_12_out, xor_13_out, xor_14_out, xor_15_out;

  xor xor_1 (xor_1_out, B7, A7);
  and and_1 (and_1_out, A6, B6);
  xor xor_2 (xor_2_out, xor_1_out, or_3_out);
  or or_1 (or_1_out, xor_2_out, not_1_out);
  _7_Segment_Display u_7_segment_display_1 (
    .f(not_1_out), .a(not_1_out), .b(or_1_out), .e(not_1_out), .d(not_1_out), .c(or_1_out));  // open: g, dp
  and and_2 (and_2_out, B6, or_6_out);
  and and_3 (and_3_out, A6, or_6_out);
  not not_1 (not_1_out, xor_2_out);
  or or_2 (or_2_out, and_3_out, and_2_out);
  or or_3 (or_3_out, and_1_out, or_2_out);
  xor xor_3 (xor_3_out, B6, A6);
  and and_4 (and_4_out, A5, or_9_out);
  xor xor_4 (xor_4_out, xor_3_out, or_6_out);
  not not_2 (not_2_out, xor_4_out);
  or or_4 (or_4_out, xor_4_out, not_2_out);
  _7_Segment_Display u_7_segment_display_2 (
    .f(not_2_out), .a(not_2_out), .b(or_4_out), .e(not_2_out), .d(not_2_out), .c(or_4_out));  // open: g, dp
  and and_5 (and_5_out, A5, A5);
  and and_6 (and_6_out, B5, or_9_out);
  or or_5 (or_5_out, and_6_out, and_5_out);
  or or_6 (or_6_out, and_4_out, or_5_out);
  xor xor_5 (xor_5_out, B5, A5);
  _7_Segment_Display u_7_segment_display_3 (
    .f(not_3_out), .a(not_3_out), .b(or_7_out), .e(not_3_out), .d(not_3_out), .c(or_7_out));  // open: g, dp
  and and_7 (and_7_out, A4, B4);
  and and_8 (and_8_out, B4, or_10_out);
  and and_9 (and_9_out, A4, or_10_out);
  xor xor_6 (xor_6_out, xor_5_out, or_9_out);
  not not_3 (not_3_out, xor_6_out);
  or or_7 (or_7_out, xor_6_out, not_3_out);
  xor xor_7 (xor_7_out, B4, A4);
  or or_8 (or_8_out, and_9_out, and_8_out);
  or or_9 (or_9_out, and_7_out, or_8_out);
  _7_Segment_Display u_7_segment_display_4 (
    .f(not_4_out), .a(not_4_out), .b(or_11_out), .e(not_4_out), .d(not_4_out), .c(or_11_out));  // open: g, dp
  and and_10 (and_10_out, A3, B3);
  and and_11 (and_11_out, A3, or_15_out);
  xor xor_8 (xor_8_out, xor_7_out, or_10_out);
  or or_10 (or_10_out, and_11_out, or_12_out);
  not not_4 (not_4_out, xor_8_out);
  or or_11 (or_11_out, xor_8_out, not_4_out);
  xor xor_9 (xor_9_out, B3, A3);
  and and_12 (and_12_out, B3, or_15_out);
  or or_12 (or_12_out, and_12_out, and_10_out);
  and and_13 (and_13_out, A2, B2);
  xor xor_10 (xor_10_out, xor_9_out, or_15_out);
  or or_13 (or_13_out, xor_10_out, not_5_out);
  _7_Segment_Display u_7_segment_display_5 (
    .f(not_5_out), .a(not_5_out), .b(or_13_out), .e(not_5_out), .d(not_5_out), .c(or_13_out));  // open: g, dp
  and and_14 (and_14_out, B2, or_18_out);
  and and_15 (and_15_out, A2, or_18_out);
  not not_5 (not_5_out, xor_10_out);
  or or_14 (or_14_out, and_15_out, and_14_out);
  or or_15 (or_15_out, and_13_out, or_14_out);
  xor xor_11 (xor_11_out, B2, A2);
  and and_16 (and_16_out, and_19_out, A1);
  xor xor_12 (xor_12_out, xor_11_out, or_18_out);
  not not_6 (not_6_out, xor_12_out);
  or or_16 (or_16_out, xor_12_out, not_6_out);
  _7_Segment_Display u_7_segment_display_6 (
    .f(not_6_out), .a(not_6_out), .b(or_16_out), .e(not_6_out), .d(not_6_out), .c(or_16_out));  // open: g, dp
  and and_17 (and_17_out, A1, B1);
  and and_18 (and_18_out, B1, and_19_out);
  or or_17 (or_17_out, and_18_out, and_17_out);
  or or_18 (or_18_out, and_16_out, or_17_out);
  xor xor_13 (xor_13_out, B1, A1);
  xor xor_14 (xor_14_out, xor_13_out, and_19_out);
  or or_19 (or_19_out, xor_14_out, not_7_out);
  _7_Segment_Display u_7_segment_display_7 (
    .f(not_7_out), .a(not_7_out), .b(or_19_out), .e(not_7_out), .d(not_7_out), .c(or_19_out));  // open: g, dp
  and and_19 (and_19_out, A0, B0);
  not not_7 (not_7_out, xor_14_out);
  xor xor_15 (xor_15_out, B0, A0);
  not not_8 (not_8_out, xor_15_out);
  or or_20 (or_20_out, xor_15_out, not_8_out);
  _7_Segment_Display u_7_segment_display_8 (
    .f(not_8_out), .a(not_8_out), .b(or_20_out), .e(not_8_out), .d(not_8_out), .c(or_20_out));  // open: g, dp
endmodule
