// Logisim project MUX.circ as structural Verilog: 2 circuits, main circuit MUX
module MUX (
  input  [1:0] in_1,
  input  [7:0] in_2,
  input  [7:0] in_3,
  input  [7:0] in_4,
  input  [7:0] in_5,
  input  [7:0] in_6,
  input  [7:0] in_7,
  input  [7:0] in_8,
  input  [7:0] in_9,
  input  [1:0] in_10,
  output [7:0] out_11,
  output [7:0] out_12
);

  wire and_1_out, and_2_out, and_3_out, and_4_out, not_1_out, not_2_out;

  not not_1 (not_1_out, in_10[0]);
  not not_2 (not_2_out, in_10[1]);
  Multiplexer #(.select(2), .width(8)) multiplexer_1 (
    .in0(in_2), .in1(in_3), .in2(in_4), .in3(in_5), .out(out_11));  // open: sel
  and and_1 (and_1_out, in_10[0], in_10[1]);
  and and_2 (and_2_out, in_10[0], not_2_out);
  and and_3 (and_3_out, not_1_out, in_10[1]);
  and and_4 (and_4_out, not_2_out, not_1_out);
  Basic_MUX basic_mux_1 (
    .D0(in_6[0]), .D1(in_7[0]), .D2(in_8[0]), .D3(in_9[0]), .Select1(and_1_out), .Select2(and_2_out),
    .Select3(and_3_out), .Select4(and_4_out), .Y(out_12[0]));
  Basic_MUX basic_mux_2 (
    .D0(in_6[2]), .D1(in_7[2]), .D2(in_8[2]), .D3(in_9[2]), .Select1(and_1_out), .Select2(and_2_out),
    .Select3(and_3_out), .Select4(and_4_out), .Y(out_12[2]));
  Basic_MUX basic_mux_3 (
    .D0(in_6[4]), .D1(in_7[4]), .D2(in_8[4]), .D3(in_9[4]), .Select1(and_1_out), .Select2(and_2_out),
    .Select3(and_3_out), .Select4(and_4_out), .Y(out_12[4]));
  Basic_MUX basic_mux_4 (
    .D0(in_6[6]), .D1(in_7[6]), .D2(in_8[6]), .D3(in_9[6]), .Select1(and_1_out), .Select2(and_2_out),
    .Select3(and_3_out), .Select4(and_4_out), .Y(out_12[6]));
  Basic_MUX basic_mux_5 (
    .D0(in_6[1]), .D1(in_7[1]), .D2(in_8[1]), .D3(in_9[1]), .Select1(and_1_out), .Select2(and_2_out),
    .Select3(and_3_out), .Select4(and_4_out), .Y(out_12[1]));
  Basic_MUX basic_mux_6 (
    .D0(in_6[3]), .D1(in_7[3]), .D2(in_8[3]), .D3(in_8[4]), .Select1(and_1_out), .Select2(and_2_out),
    .Select3(and_3_out), .Select4(and_4_out), .Y(out_12[3]));
  Basic_MUX basic_mux_7 (
    .D0(in_6[5]), .D1(in_7[5]), .D2(in_8[5]), .D3(in_9[5]), .Select1(and_1_out), .Select2(and_2_out),
    .Select3(and_3_out), .Select4(and_4_out), .Y(out_12[5]));
  Basic_MUX basic_mux_8 (
    .D0(in_6[7]), .D1(in_7[7]), .D2(in_8[7]), .D3(in_9[7]), .Select1(and_1_out), .Select2(and_2_out),
    .Select3(and_3_out), .Select4(and_4_out), .Y(out_12[7]));

  assign in_9[3] = in_8[4];
endmodule

module Basic_MUX (
  input  D0,
  input  D1,
  input  D2,
  input  D3,
  input  Select1,
  input  Select2,
  input  Select3,
  input  Select4,
  output Y
);

  wire and_1_out, and_2_out, and_3_out, and_4_out;

  and and_1 (and_1_out, D0, Select1);
  and and_2 (and_2_out, D1, Select2);
  and and_3 (and_3_out, D2, Select3);
  and and_4 (and_4_out, D3, Select4);
  or or_1 (Y, and_1_out, and_2_out, and_3_out, and_4_out);
endmodule
