// Logisim project RippleAdder.circ as structural Verilog: 2 circuits, main circuit RippeAdder
module RippeAdder (
  input  [7:0] A,
  input  [7:0] B,
  output [7:0] out_3,
  output Overflow
);

  wire fulladder_1_cout, fulladder_2_cout, fulladder_3_cout, fulladder_4_cout, fulladder_5_cout,
       fulladder_6_cout, fulladder_7_cout;

  FullAdder fulladder_1 (.in_2(A[0]), .in_3(B[0]), .out_4(out_3[0]), .cout(fulladder_1_cout));  // open: Cin
  FullAdder fulladder_2 (.Cin(fulladder_1_cout), .in_2(A[1]), .in_3(B[1]), .out_4(out_3[1]), .cout(fulladder_2_cout));
  FullAdder fulladder_3 (.Cin(fulladder_2_cout), .in_2(A[2]), .in_3(B[2]), .out_4(out_3[2]), .cout(fulladder_3_cout));
  FullAdder fulladder_4 (.Cin(fulladder_3_cout), .in_2(A[3]), .in_3(B[3]), .out_4(out_3[3]), .cout(fulladder_4_cout));
  FullAdder fulladder_5 (.Cin(fulladder_4_cout), .in_2(A[4]), .in_3(B[4]), .out_4(out_3[4]), .cout(fulladder_5_cout));
  FullAdder fulladder_6 (.Cin(fulladder_5_cout), .in_2(A[5]), .in_3(B[5]), .out_4(out_3[5]), .cout(fulladder_6_cout));
  FullAdder fulladder_7 (.Cin(fulladder_6_cout), .in_2(A[6]), .in_3(B[6]), .out_4(out_3[6]), .cout(fulladder_7_cout));
  FullAdder fulladder_8 (.Cin(fulladder_7_cout), .in_2(A[7]), .in_3(B[7]), .out_4(out_3[7]), .cout(Overflow));
endmodule

module FullAdder (
  input  Cin,
  input  in_2,
  input  in_3,
  output out_4,
  output cout
);

  wire and_1_out, and_2_out, or_1_out, xor_1_out;

  xor xor_1 (xor_1_out, in_2, in_3);
  and and_1 (and_1_out, in_3, in_2);
  xor xor_2 (out_4, Cin, xor_1_out);
  or or_1 (or_1_out, in_3, in_2);
  and and_2 (and_2_out, Cin, or_1_out);
  or or_2 (cout, and_2_out, and_1_out);
endmodule
