// Logisim project Tutoriall.circ as structural Verilog: 1 circuit, main circuit main
module main (
  input  A,
  input  B,
  input  X,
  input  Y,
  input  M,
  input  N,
  input  E,
  input  F
);

  wire and_1_out, and_2_out, and_3_out, not_1_out, not_2_out, not_3_out, not_4_out, not_5_out, or_1_out,
       or_2_out, xor_1_out;

  not not_1 (not_1_out, X);
  not not_2 (not_2_out, Y);
  not not_3 (not_3_out, E);
  not not_4 (not_4_out, F);
  and and_1 (and_1_out, not_3_out, not_4_out);
  xor xor_1 (xor_1_out, A, B);
  and and_2 (and_2_out, X, not_2_out);
  and and_3 (and_3_out, not_1_out, Y);
  or or_1 (or_1_out, M, N);
  LED P (.in(or_1_out));
  not not_5 (not_5_out, and_1_out);
  LED G (.in(not_5_out));
  LED C (.in(xor_1_out));
  or or_2 (or_2_out, and_2_out, and_3_out);
  LED Z (.in(or_2_out));
endmodule
